# Fritzing sketch control_electronics (saved by Fritzing 0.9.3b)
perfboards: 1

parts:
  DC_JACK = Power Jack [package=power_jack_slot]
  Part1 = Arduino Uno (Rev3)
  U1 = LM2596 step down module
  IC1 = L293D [package=THT]
  M1 = DC Motor
  OLED1 = OLED 128x64 I2C Monochrome Display
  Toggle_Switch = Toggle Switch [package=THT]
  R1 = Rotary Potentiometer (Large) [maximum_resistance=10kΩ package=THT]

nets:
  GND: DC_JACK.GNDBREAK, DC_JACK.GND, Part1.GND, U1.IN-, U1.OUT-, IC1.0V, OLED1.GND, Toggle_Switch.COM, R1.leg1
  N1: DC_JACK.PWR, U1.IN+, IC1.+Vmotor
  N2: Part1.A0, R1.wiper
  N3: Part1.D8, Toggle_Switch.L1
  N4: Part1.D11_PWM/MOSI, IC1.Enable_1
  N5: Part1.D12/MISO, IC1.In_1
  N6: Part1.D13/SCK, IC1.In_2
  N7: Part1.A4/SDA, OLED1.SDA
  N8: Part1.A5/SCL, OLED1.SCK
  N9: Part1.D7, Toggle_Switch.L2
  VIN: Part1.VIN, U1.OUT+, OLED1.VDD, R1.leg2
  N10: IC1.Out_1_(_Controlled_by_Enable_1_), M1.pin_2
  N11: IC1.Out_2_(_Controlled_by_Enable_1_), M1.pin_1

notes:
  12 V
  5 V
  Motor 1
  DC Port
  Motor Driver
  OLED
  Flow Rate Pot.
  Toggle Switch

custom parts:
  LM2596 step down module: LM2596 DC-DC step down power supply module 3 A.
