# Fritzing sketch flow_meter (saved by Fritzing 0.9.3b)

parts:
  Raspberry_Pi_1 = Raspberry Pi 3 [part_number=RPI-3-V1.2]
  YF-S201_Flow_Meter1 = YF-S201 Water Flow Meter

nets:
  3V3: Raspberry_Pi_1.3v3, YF-S201_Flow_Meter1.VCC
  N1: Raspberry_Pi_1.GPIO4, YF-S201_Flow_Meter1.SIG
  GND: Raspberry_Pi_1.GND, YF-S201_Flow_Meter1.GND

custom parts:
  YF-S201 Water Flow Meter: The YF-S201 Flow Meter. The input voltage is 5V to 24V (DC).
